# Fritzing sketch pcb (saved by Fritzing 0.9.3b)
circuit board: 9cm x 6cm
breadboards: 2

parts:
  WeMos_D1_Mini1 = WeMos D1 Mini
  U1_LB_On = RELAY [package=relay-g5q]
  U2_LB_Clear = RELAY [package=relay-g5q]
  U3_Trigger = RELAY [package=relay-g5q]
  T1 = NPN-Transistor [package="TO92 [THT]"]
  Q2 = PNP-Transistor [package="TO92 [THT]"]
  J1_Gate_Trigger = Screw terminal - 2 pins [package=THT]
  J2_LB_12V/Clear/Blocked/GND = screw terminal, 4 pins
  S1 = Toggle Switch [package=THT]
  J3_Autoclose_Button = Screw terminal - 2 pins [package=THT]
  T2 = NPN-Transistor [package="TO92 [THT]"]
  C1 = Electrolytic Capacitor [capacitance=100µF package="100 mil [THT, electrolytic]"]
  R1 = Resistor [tolerance=±5% resistance=220 package=THT]
  R2 = Resistor [tolerance=±5% resistance=220 package=THT]
  Q3 = PNP-Transistor [package="TO92 [THT]"]
  R4 = Resistor [tolerance=±5% resistance=220 package=THT]
  Q4 = NPN-Transistor [package="TO92 [THT]"]
  Q5 = NPN-Transistor [package="TO92 [THT]"]
  R5 = Resistor [tolerance=±5% resistance=220 package=THT]
  J4_Gate_Up/Down_Sensors = screw terminal, 3 pins
  U4 = Voltage Regulator - 5V [package="TO220 [THT]"]
  R3 = Resistor [tolerance=±5% resistance=220 package=THT]

nets:
  N1: WeMos_D1_Mini1.3V3, R1.Pin_0, R2.Pin_0, R4.Pin_0, R5.Pin_0, R3.Pin_0
  N2: WeMos_D1_Mini1.5V, U1_LB_On.COIL2, U2_LB_Clear.COIL1, U3_Trigger.COIL1, C1.+, U4.output_voltage
  N3: WeMos_D1_Mini1.D0, Q4.C, R5.Pin_1
  N4: WeMos_D1_Mini1.D1, Q2.B, R2.Pin_1, J4_Gate_Up/Down_Sensors.pin1
  N5: WeMos_D1_Mini1.D2, R1.Pin_1, Q3.B, J4_Gate_Up/Down_Sensors.pin2
  N6: WeMos_D1_Mini1.D3, J3_Autoclose_Button.pin1
  N7: WeMos_D1_Mini1.D5, T2.B
  N8: WeMos_D1_Mini1.D6, J2_LB_12V/Clear/Blocked/GND.pin3, S1.L2
  N9: WeMos_D1_Mini1.D7, U2_LB_Clear.COIL2, J2_LB_12V/Clear/Blocked/GND.pin2, S1.L1
  N10: WeMos_D1_Mini1.D8, T1.B
  GND: WeMos_D1_Mini1.G, T1.E, J2_LB_12V/Clear/Blocked/GND.pin4, S1.COM, J3_Autoclose_Button.pin2, T2.E, C1.-, Q5.E, J4_Gate_Up/Down_Sensors.pin3, U4.GND
  N11: U1_LB_On.MAIN, J2_LB_12V/Clear/Blocked/GND.pin1
  12V: U1_LB_On.NO, U4.input_voltage
  N12: U1_LB_On.COIL1, T1.C
  N13: U2_LB_Clear.MAIN, J1_Gate_Trigger.pin2
  N14: U2_LB_Clear.NO, U3_Trigger.MAIN
  N15: U3_Trigger.COIL2, T2.C
  N16: U3_Trigger.NO, J1_Gate_Trigger.pin1
  N17: Q2.E, R3.Pin_1
  N18: Q2.C, Q4.B
  N19: Q3.E, R4.Pin_1
  N20: Q3.C, Q5.B
  N21: Q4.E, Q5.C
